# Fritzing sketch schematics (saved by Fritzing 0.9.2b)
breadboards: 1

parts:
  Part1 = Arduino Uno (Rev3)
  LED1 = LED - 5mm [color="Green (555nm)" package="5 mm [THT]"]
  LED2 = LED - 5mm [color="Blue (430nm)" package="5 mm [THT]"]
  LED3 = LED - 5mm [color="Red (633nm)" package="5 mm [THT]"]
  R1 = Resistor [tolerance=±5% resistance=220 package=THT]
  R2 = Resistor [tolerance=±5% resistance=220 package=THT]
  R3 = Resistor [tolerance=±5% resistance=220 package=THT]

nets:
  N1: Part1.D9_PWM, LED1.anode
  N2: Part1.D10_PWM/SS, LED2.anode
  N3: Part1.GND, R1.Pin_1, R2.Pin_1, R3.Pin_1
  N4: Part1.D6_PWM, LED3.anode
  N5: LED1.cathode, R2.Pin_0
  N6: LED2.cathode, R1.Pin_0
  N7: LED3.cathode, R3.Pin_0
